# Fritzing sketch moisture_pi (saved by Fritzing 0.9.3b)
breadboards: 1

parts:
  Componente2 = Adafruit ADS1115 16Bit I2C ADC [part_number="Adafruit #1085"]
  R1 = Resistor [tolerance=±5% resistance=10k package=THT]
  R2 = Resistor [tolerance=±5% resistance=10k package=THT]
  R3 = Resistor [tolerance=±5% resistance=10k package=THT]
  R4 = Resistor [tolerance=±5% resistance=10k package=THT]
  J1 = female pin header, 4 pins [form="♀ (female)"]
  Componente4 = Soil Moisture Sensor

nets:
  N1: Componente2.AIN3, R4.Pin_1, J1.pin4
  N2: Componente2.AIN2, R3.Pin_1, J1.pin3
  N3: Componente2.AIN1, R2.Pin_1, J1.pin2
  N4: Componente2.AIN0, R1.Pin_1, J1.pin1, Componente4.SIG
  GND: Componente2.ADDR, Componente2.GND, Componente4.GND
  N5: Componente2.VDD, R1.Pin_0, R2.Pin_0, R3.Pin_0, R4.Pin_0

custom parts:
  Adafruit ADS1115 16Bit I2C ADC: For microcontrollers without an analog-to-digital converter or when you want a higher-precision ADC, the ADS1115 provides 16-bit precision at 860 samples/second over I2C. The chip can be configured as 4 single-ended input channels, or two differential channels. As a nice bonus, it even includes a programmable gain amplifier, up to x16, to help boost up smaller single/differential signals to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
